# Fritzing sketch SelfDrivingCar (saved by Fritzing 0.9.1b)
breadboards: 1

parts:
  Range_finder_HC-SR04 = HC-SR04 Ultrasonic Rangemeter
  Bluetooth_connection = Bluetooth Mate Silver
  IR_Receiver = TSOP312.., 314.. [package=THT]
  External_voltage_regulator = Voltage Regulator - 5V [package="TO220 [THT]"]
  Scanning_servo = Basic Servo [part_number="TowerPro SG90 - 200ma with no load"]
  Car_steering = Basic Servo [part_number="Futaba S3003, up to 400ma (stall)"]
  Car_throttle = Basic Servo [part_number="Brushed ESC"]
  Tilt_switch = Tilt Switch [package=THT]
  R3 = Resistor [tolerance=±5% resistance=10k package="0603 [SMD]"]
  R1 = Resistor [tolerance=±5% resistance=10k package="0603 [SMD]"]
  R2 = Resistor [tolerance=±5% resistance=3.3k package="0603 [SMD]"]
  To_car_battery = Power plug
  Buzzer = Piezo Speaker
  I2C_to_LCD = LCM1602 IIC [part_number="LCM1602 IIC" chip_label="LCM1602 IIC" package="DIP (Dual Inline) [THT]"]
  LCD1 = LCD screen
  Part1 = Arduino Micro (Rev3)

nets:
  VCC: Range_finder_HC-SR04.VCC, Bluetooth_connection.VCC, IR_Receiver.Vs, External_voltage_regulator.output_voltage, Scanning_servo.vcc, Car_steering.vcc, Car_throttle.vcc, Tilt_switch.Pin_1, I2C_to_LCD.VCC, Part1.5V
  N1: Range_finder_HC-SR04.Trig, Part1.A4
  N2: Range_finder_HC-SR04.Echo, Part1.A3
  GND: Range_finder_HC-SR04.GND, Bluetooth_connection.GND, IR_Receiver.GND, External_voltage_regulator.GND, Scanning_servo.gnd, Car_steering.gnd, Car_throttle.gnd, R3.Pin_0, R2.Pin_1, To_car_battery.GND, Buzzer.pin1, I2C_to_LCD.GND, Part1.GND
  N3: Bluetooth_connection.RTS_5V, Bluetooth_connection.CTS_5V
  N4: Bluetooth_connection.RX_5V, Part1.D1/TX
  N5: Bluetooth_connection.TX_5V, Part1.D0/RX
  N6: IR_Receiver.Data, Part1.D6_PWM/A7
  N7: External_voltage_regulator.input_voltage, R1.Pin_1, To_car_battery.VCC
  N8: Scanning_servo.pulse, Part1.A2
  N9: Car_steering.pulse, Part1.A0
  N10: Car_throttle.pulse, Part1.A1
  N11: Tilt_switch.Pin_2, R3.Pin_1, Part1.D7
  N12: R1.Pin_0, Part1.A5
  N13: Buzzer.pin2, Part1.D10_PWM/A10
  VSS: I2C_to_LCD.VSS, LCD1.VSS
  VDD: I2C_to_LCD.VDD, LCD1.VDD
  N14: I2C_to_LCD.V0, LCD1.V0
  N15: I2C_to_LCD.RS, LCD1.RS
  N16: I2C_to_LCD.RW, LCD1.R/W
  N17: I2C_to_LCD.E, LCD1.E
  N18: I2C_to_LCD.D0, LCD1.DB0
  N19: I2C_to_LCD.D1, LCD1.DB1
  N20: I2C_to_LCD.D2, LCD1.DB2
  N21: I2C_to_LCD.D3, LCD1.DB3
  N22: I2C_to_LCD.D4, LCD1.DB4
  N23: I2C_to_LCD.D5, LCD1.DB5
  N24: I2C_to_LCD.D6, LCD1.DB6
  N25: I2C_to_LCD.D7, LCD1.DB7
  N26: I2C_to_LCD.A, LCD1.LED+
  N27: I2C_to_LCD.K, LCD1.LED-
  N28: I2C_to_LCD.SDA, Part1.D2/SDA
  N29: I2C_to_LCD.SCL, Part1.D3/SCL

custom parts:
  LCM1602 IIC: I2C-Module to use a 1602 or 2004 LCD on with the wire.h libory Serial LCD Modul
